# Fritzing sketch rgb-led (saved by Fritzing 0.9.0b)
breadboards: 1

parts:
  Arduino = Arduino Nano (Rev3.0)
  RGB_LED = RGB LED (com. anode, rbg) [package="5 mm [THT]"]
  DC_12V = Power plug
  RB = Rotary Potentiometer (Large) [package=THT]
  RG = Rotary Potentiometer (Large) [package=THT]
  RR = Rotary Potentiometer (Large) [package=THT]
  QG = MOSFET-NCHANNEL [package=to220v]
  QB = MOSFET-NCHANNEL [package=to220v]
  QR = MOSFET-NCHANNEL [package=to220v]

nets:
  GND: Arduino.GND, DC_12V.GND, RB.leg2, RG.leg2, RR.leg2, QG.D, QB.D, QR.D
  N1: Arduino.D3, QG.G
  N2: Arduino.D5, QB.G
  N3: Arduino.D6, QR.G
  VIN: Arduino.VIN, RGB_LED.common_anode, DC_12V.VCC
  N4: Arduino.5V, RB.leg1, RG.leg1, RR.leg1
  N5: Arduino.A2, RB.wiper
  N6: Arduino.A1, RG.wiper
  N7: Arduino.A0, RR.wiper
  N8: RGB_LED.red_cathode, QR.S
  N9: RGB_LED.blue_cathode, QB.S
  N10: RGB_LED.green_cathode, QG.S

notes:
  Schema v2.1
  Breadboard Design v2.1

custom parts:
  Rotary Potentiometer (Large): A rotary adjustable resistor (potentiometer).
